# Fritzing sketch Untitled Sketch 2 (saved by Fritzing 0.9.3b)

parts:
  Part2 = Arduino Mega 2560 (Rev3)
  Matrix_keypad1 = KEYPAD 4x4
  LED1 = LED - 3mm [color="Red (633nm)" package="3 mm [THT]"]

nets:
  N1: Part2.GND, LED1.cathode
  N2: Part2.D13_PWM, LED1.anode
  N3: Part2.D0_RX0, Matrix_keypad1.row4
  N4: Part2.D1_TX0, Matrix_keypad1.row3
  N5: Part2.D2_PWM, Matrix_keypad1.row2
  N6: Part2.D3_PWM, Matrix_keypad1.row1
  N7: Part2.D4_PWM, Matrix_keypad1.col4
  N8: Part2.D5_PWM, Matrix_keypad1.col3
  N9: Part2.D6_PWM, Matrix_keypad1.col2
  N10: Part2.D7_PWM, Matrix_keypad1.col1

custom parts:
  KEYPAD 4x4: Matrix keypad 16 buttons, 4 rows x 4 columns
