# Fritzing sketch Untitled Sketch 3 (saved by Fritzing 0.9.3b)
breadboards: 1

parts:
  Part1 = Arduino Uno (Rev3) - ICSP
  U1 = POT [package=pot_alpha_rv16af-20]  # not connected
  LED1 = LED - 3mm [color="Infrared (880nm)" package="3 mm [THT]"]  # not connected
  U2 = LM358 [package=dip08]
  R1 = Resistor [tolerance=±5% resistance=220 package="2512 [SMD]"]
  J1 = Basic Servo
  S1 = H-Bridge with L298N
  M1 = DC Motor

nets:
  N1: Part1.D8, S1.IN1
  GND: Part1.GND, J1.gnd, S1.GND
  N2: Part1.D2, U2.G$2_-IN
  N3: Part1.D3_PWM, J1.pulse
  VIN: Part1.VIN, J1.vcc
  N4: U2.G$1_-IN, R1.Pin_1
  N5: S1.M1-01, M1.pin_1
  N6: S1.M1-02, M1.pin_2

notes:
  12 V

custom parts:
  H-Bridge with L298N: h-bridge
